# Fritzing sketch Sketch_pushButton (saved by Fritzing 0.9.2b)
circuit board: 13.8966cm x 8.80182cm
breadboards: 1

parts:
  Raspberry_Pi1 = Raspberry Pi 2
  LED1 = LED - 5mm [color="Red (633nm)" package="5 mm [THT]"]
  R1 = Resistor [tolerance=±5% resistance=220 package=THT]
  S1 = Pushbutton [package="[THT]"]
  R2 = Resistor [tolerance=±5% resistance=220 package=THT]

nets:
  N1: Raspberry_Pi1.GPIO17, LED1.anode
  N2: Raspberry_Pi1.GPIO10, S1.Pin_3, S1.Pin_4, R2.Pin_0
  N3: Raspberry_Pi1.GND, R1.Pin_0, S1.Pin_1, S1.Pin_2
  N4: Raspberry_Pi1.5V, R2.Pin_1
  N5: LED1.cathode, R1.Pin_1
